// Logisim project Basic_RAM.circ as structural Verilog: 1 circuit, main circuit main
module main (
  input  Address_2,
  input  Address_1,
  input  Address_0,
  input  In_3,
  input  In_2,
  input  In_1,
  input  In_0,
  input  Mode,
  output Out_3,
  output Out_2,
  output Out_1,
  output Out_0
);

  wire and_1_out, and_2_out, and_3_out, and_4_out, and_5_out, and_6_out, and_7_out, and_8_out, and_9_out,
       and_10_out, and_11_out, and_12_out, and_13_out, and_14_out, and_15_out, and_16_out, and_17_out,
       and_18_out, and_19_out, and_20_out, and_21_out, and_22_out, and_23_out, and_24_out, and_25_out,
       and_26_out, and_27_out, and_28_out, and_29_out, and_30_out, and_31_out, and_32_out, and_33_out,
       and_34_out, and_35_out, and_36_out, and_37_out, and_38_out, and_39_out, and_40_out, and_41_out,
       and_42_out, and_43_out, and_44_out, and_45_out, and_46_out, and_47_out, and_48_out, and_49_out,
       and_50_out, and_51_out, and_52_out, and_53_out, and_54_out, and_55_out, and_56_out, clock_1_out,
       d_ff_1_q, d_ff_1_qn, d_ff_2_q, d_ff_2_qn, d_ff_3_q, d_ff_3_qn, d_ff_4_q, d_ff_4_qn, d_ff_5_q,
       d_ff_6_q, d_ff_7_q, d_ff_8_q, d_ff_9_q, d_ff_10_q, d_ff_11_q, d_ff_12_q, d_ff_14_q, d_ff_16_q,
       d_ff_17_q, d_ff_18_q, d_ff_19_q, d_ff_20_q, d_ff_21_q, d_ff_22_q, d_ff_23_q, d_ff_24_q, d_ff_26_q,
       d_ff_28_q, d_ff_29_q, d_ff_30_q, d_ff_31_q, d_ff_32_q, d_ff_33_q, d_ff_34_q, d_ff_35_q, d_ff_36_q,
       d_ff_37_q, d_ff_38_q, d_ff_39_q, d_ff_40_q, d_ff_41_q, d_ff_42_q, d_ff_43_q, d_ff_44_q, or_1_out,
       or_2_out, or_3_out, or_4_out, or_5_out;

  D_Flip_Flop d_ff_1 (.D(Address_2), .clk(clock_1_out), .Q(d_ff_1_q), .Qn(d_ff_1_qn));  // open: preset, reset
  D_Flip_Flop #(.trigger("falling")) d_ff_2 (
    .D(Address_1), .clk(clock_1_out), .Q(d_ff_2_q), .Qn(d_ff_2_qn));  // open: preset, reset
  D_Flip_Flop d_ff_3 (.D(Address_0), .clk(clock_1_out), .Q(d_ff_3_q), .Qn(d_ff_3_qn));  // open: preset, reset
  and and_1 (and_1_out, d_ff_1_qn, d_ff_2_qn, d_ff_3_qn);
  and and_2 (and_2_out, d_ff_1_qn, d_ff_2_qn, d_ff_3_q);
  and and_3 (and_3_out, d_ff_1_qn, d_ff_2_q, d_ff_3_qn);
  and and_4 (and_4_out, d_ff_1_qn, d_ff_2_q, d_ff_3_q);
  and and_5 (and_5_out, d_ff_1_q, d_ff_2_qn, d_ff_3_qn);
  and and_6 (and_6_out, d_ff_1_q, d_ff_2_qn, d_ff_3_q);
  and and_7 (and_7_out, d_ff_1_q, d_ff_2_q, d_ff_3_qn);
  and and_8 (and_8_out, d_ff_1_q, d_ff_2_q, d_ff_3_q);
  and and_9 (and_9_out, clock_1_out, and_1_out, or_1_out);
  and and_10 (and_10_out, clock_1_out, and_2_out, or_1_out);
  and and_11 (and_11_out, clock_1_out, and_3_out, or_1_out);
  and and_12 (and_12_out, clock_1_out, and_4_out, or_1_out);
  and and_13 (and_13_out, clock_1_out, and_5_out, or_1_out);
  and and_14 (and_14_out, clock_1_out, and_6_out, or_1_out);
  and and_15 (and_15_out, clock_1_out, and_7_out, or_1_out);
  and and_16 (and_16_out, clock_1_out, and_8_out, or_1_out);
  Clock clock_1 (.out(clock_1_out));
  D_Flip_Flop d_ff_4 (.D(Mode), .clk(clock_1_out), .Q(d_ff_4_q), .Qn(d_ff_4_qn));  // open: preset, reset
  or or_1 (or_1_out, d_ff_4_q, d_ff_4_qn);
  D_Flip_Flop #(.trigger("falling")) d_ff_5 (.clk(and_9_out), .D(d_ff_14_q), .Q(d_ff_5_q));  // open: Qn, preset, reset
  D_Flip_Flop #(.trigger("falling")) d_ff_6 (.clk(and_10_out), .D(d_ff_14_q), .Q(d_ff_6_q));  // open: Qn, preset, reset
  D_Flip_Flop #(.trigger("falling")) d_ff_7 (.clk(and_11_out), .D(d_ff_14_q), .Q(d_ff_7_q));  // open: Qn, preset, reset
  D_Flip_Flop #(.trigger("falling")) d_ff_8 (.clk(and_12_out), .D(d_ff_14_q), .Q(d_ff_8_q));  // open: Qn, preset, reset
  D_Flip_Flop #(.trigger("falling")) d_ff_9 (.clk(and_13_out), .D(d_ff_14_q), .Q(d_ff_9_q));  // open: Qn, preset, reset
  D_Flip_Flop #(.trigger("falling")) d_ff_10 (
    .clk(and_14_out), .D(d_ff_14_q), .Q(d_ff_10_q));  // open: Qn, preset, reset
  D_Flip_Flop #(.trigger("falling")) d_ff_11 (
    .clk(and_15_out), .D(d_ff_14_q), .Q(d_ff_11_q));  // open: Qn, preset, reset
  D_Flip_Flop #(.trigger("falling")) d_ff_12 (
    .clk(and_16_out), .D(d_ff_14_q), .Q(d_ff_12_q));  // open: Qn, preset, reset
  D_Flip_Flop #(.trigger("falling")) d_ff_13 (.D(and_17_out), .clk(or_1_out), .Q(Out_3));  // open: Qn, preset, reset
  and and_17 (and_17_out, Mode, and_18_out);
  and and_18 (and_18_out, d_ff_4_q, or_2_out);
  or or_2 (or_2_out, and_19_out, and_20_out, and_21_out, and_22_out, and_23_out, and_24_out, and_25_out, and_26_out);
  and and_19 (and_19_out, and_9_out, d_ff_5_q);
  and and_20 (and_20_out, and_10_out, d_ff_6_q);
  and and_21 (and_21_out, and_11_out, d_ff_7_q);
  and and_22 (and_22_out, and_12_out, d_ff_8_q);
  and and_23 (and_23_out, and_13_out, d_ff_9_q);
  and and_24 (and_24_out, and_14_out, d_ff_10_q);
  and and_25 (and_25_out, and_15_out, d_ff_11_q);
  and and_26 (and_26_out, and_16_out, d_ff_12_q);
  D_Flip_Flop d_ff_14 (.D(In_3), .clk(clock_1_out), .Q(d_ff_14_q));  // open: Qn, preset, reset
  D_Flip_Flop d_ff_15 (.D(and_27_out), .clk(or_1_out), .Q(Out_2));  // open: Qn, preset, reset
  and and_27 (and_27_out, Mode, and_28_out);
  and and_28 (and_28_out, d_ff_4_q, or_3_out);
  D_Flip_Flop #(.trigger("falling")) d_ff_16 (
    .clk(and_9_out), .D(d_ff_24_q), .Q(d_ff_16_q));  // open: Qn, preset, reset
  D_Flip_Flop #(.trigger("falling")) d_ff_17 (
    .clk(and_10_out), .D(d_ff_24_q), .Q(d_ff_17_q));  // open: Qn, preset, reset
  D_Flip_Flop #(.trigger("falling")) d_ff_18 (
    .clk(and_11_out), .D(d_ff_24_q), .Q(d_ff_18_q));  // open: Qn, preset, reset
  D_Flip_Flop #(.trigger("falling")) d_ff_19 (
    .clk(and_12_out), .D(d_ff_24_q), .Q(d_ff_19_q));  // open: Qn, preset, reset
  D_Flip_Flop #(.trigger("falling")) d_ff_20 (
    .clk(and_13_out), .D(d_ff_24_q), .Q(d_ff_20_q));  // open: Qn, preset, reset
  D_Flip_Flop #(.trigger("falling")) d_ff_21 (
    .clk(and_14_out), .D(d_ff_24_q), .Q(d_ff_21_q));  // open: Qn, preset, reset
  D_Flip_Flop #(.trigger("falling")) d_ff_22 (
    .clk(and_15_out), .D(d_ff_24_q), .Q(d_ff_22_q));  // open: Qn, preset, reset
  D_Flip_Flop #(.trigger("falling")) d_ff_23 (
    .clk(and_16_out), .D(d_ff_24_q), .Q(d_ff_23_q));  // open: Qn, preset, reset
  D_Flip_Flop d_ff_24 (.D(In_2), .clk(clock_1_out), .Q(d_ff_24_q));  // open: Qn, preset, reset
  D_Flip_Flop d_ff_25 (.D(and_29_out), .clk(or_1_out), .Q(Out_1));  // open: Qn, preset, reset
  and and_29 (and_29_out, Mode, and_30_out);
  and and_30 (and_30_out, d_ff_4_q, or_4_out);
  or or_3 (or_3_out, and_31_out, and_32_out, and_33_out, and_34_out, and_35_out, and_36_out, and_37_out, and_38_out);
  and and_31 (and_31_out, and_9_out, d_ff_16_q);
  and and_32 (and_32_out, and_10_out, d_ff_17_q);
  and and_33 (and_33_out, and_11_out, d_ff_18_q);
  and and_34 (and_34_out, and_12_out, d_ff_19_q);
  and and_35 (and_35_out, and_13_out, d_ff_20_q);
  and and_36 (and_36_out, and_14_out, d_ff_21_q);
  and and_37 (and_37_out, and_15_out, d_ff_22_q);
  and and_38 (and_38_out, and_16_out, d_ff_23_q);
  D_Flip_Flop d_ff_26 (.D(In_1), .clk(clock_1_out), .Q(d_ff_26_q));  // open: Qn, preset, reset
  D_Flip_Flop d_ff_27 (.D(and_39_out), .clk(or_1_out), .Q(Out_0));  // open: Qn, preset, reset
  and and_39 (and_39_out, Mode, and_40_out);
  and and_40 (and_40_out, d_ff_4_q, or_5_out);
  D_Flip_Flop d_ff_28 (.D(In_0), .clk(clock_1_out), .Q(d_ff_28_q));  // open: Qn, preset, reset
  and and_41 (and_41_out, and_9_out, d_ff_29_q);
  D_Flip_Flop #(.trigger("falling")) d_ff_29 (
    .clk(and_9_out), .D(d_ff_26_q), .Q(d_ff_29_q));  // open: Qn, preset, reset
  and and_42 (and_42_out, and_10_out, d_ff_30_q);
  D_Flip_Flop #(.trigger("falling")) d_ff_30 (
    .clk(and_10_out), .D(d_ff_26_q), .Q(d_ff_30_q));  // open: Qn, preset, reset
  and and_43 (and_43_out, and_11_out, d_ff_31_q);
  D_Flip_Flop #(.trigger("falling")) d_ff_31 (
    .clk(and_11_out), .D(d_ff_26_q), .Q(d_ff_31_q));  // open: Qn, preset, reset
  and and_44 (and_44_out, and_12_out, d_ff_32_q);
  D_Flip_Flop #(.trigger("falling")) d_ff_32 (
    .clk(and_12_out), .D(d_ff_26_q), .Q(d_ff_32_q));  // open: Qn, preset, reset
  and and_45 (and_45_out, and_13_out, d_ff_33_q);
  D_Flip_Flop #(.trigger("falling")) d_ff_33 (
    .clk(and_13_out), .D(d_ff_26_q), .Q(d_ff_33_q));  // open: Qn, preset, reset
  and and_46 (and_46_out, and_14_out, d_ff_34_q);
  D_Flip_Flop #(.trigger("falling")) d_ff_34 (
    .clk(and_14_out), .D(d_ff_26_q), .Q(d_ff_34_q));  // open: Qn, preset, reset
  and and_47 (and_47_out, and_15_out, d_ff_35_q);
  D_Flip_Flop #(.trigger("falling")) d_ff_35 (
    .clk(and_15_out), .D(d_ff_26_q), .Q(d_ff_35_q));  // open: Qn, preset, reset
  and and_48 (and_48_out, and_16_out, d_ff_36_q);
  D_Flip_Flop #(.trigger("falling")) d_ff_36 (
    .clk(and_16_out), .D(d_ff_26_q), .Q(d_ff_36_q));  // open: Qn, preset, reset
  or or_4 (or_4_out, and_41_out, and_42_out, and_43_out, and_44_out, and_45_out, and_46_out, and_47_out, and_48_out);
  and and_49 (and_49_out, and_9_out, d_ff_37_q);
  D_Flip_Flop #(.trigger("falling")) d_ff_37 (
    .clk(and_9_out), .D(d_ff_28_q), .Q(d_ff_37_q));  // open: Qn, preset, reset
  and and_50 (and_50_out, and_10_out, d_ff_38_q);
  D_Flip_Flop #(.trigger("falling")) d_ff_38 (
    .clk(and_10_out), .D(d_ff_28_q), .Q(d_ff_38_q));  // open: Qn, preset, reset
  and and_51 (and_51_out, and_11_out, d_ff_39_q);
  D_Flip_Flop #(.trigger("falling")) d_ff_39 (
    .clk(and_11_out), .D(d_ff_28_q), .Q(d_ff_39_q));  // open: Qn, preset, reset
  and and_52 (and_52_out, and_12_out, d_ff_40_q);
  D_Flip_Flop #(.trigger("falling")) d_ff_40 (
    .clk(and_12_out), .D(d_ff_28_q), .Q(d_ff_40_q));  // open: Qn, preset, reset
  and and_53 (and_53_out, and_13_out, d_ff_41_q);
  D_Flip_Flop #(.trigger("falling")) d_ff_41 (
    .clk(and_13_out), .D(d_ff_28_q), .Q(d_ff_41_q));  // open: Qn, preset, reset
  and and_54 (and_54_out, and_14_out, d_ff_42_q);
  D_Flip_Flop #(.trigger("falling")) d_ff_42 (
    .clk(and_14_out), .D(d_ff_28_q), .Q(d_ff_42_q));  // open: Qn, preset, reset
  and and_55 (and_55_out, and_15_out, d_ff_43_q);
  D_Flip_Flop #(.trigger("falling")) d_ff_43 (
    .clk(and_15_out), .D(d_ff_28_q), .Q(d_ff_43_q));  // open: Qn, preset, reset
  and and_56 (and_56_out, and_16_out, d_ff_44_q);
  D_Flip_Flop #(.trigger("falling")) d_ff_44 (
    .clk(and_16_out), .D(d_ff_28_q), .Q(d_ff_44_q));  // open: Qn, preset, reset
  or or_5 (or_5_out, and_49_out, and_50_out, and_51_out, and_52_out, and_53_out, and_54_out, and_55_out, and_56_out);

  // Notes on the sheet:
  //   Row Selector Circuit
  //   Address Register
  //   Mode Register
  //   Data-Out Register
  //   Data-In Register
  //   8-nibbles RAM
endmodule
