// Logisim project basic_ALU.circ as structural Verilog: 2 circuits, main circuit ALU
module ALU (
  input  L_In_S,
  input  L_In_2,
  input  L_In_1,
  input  L_In_0,
  input  R_In_S,
  input  R_In_2,
  input  R_In_1,
  input  R_In_0,
  input  Add_Sub_Command,
  output Negative,
  output Zero,
  output Magnitude_Overflow,
  output A_Out_S,
  output A_Out_2,
  output A_Out_1,
  output A_Out_0
);

  wire and_1_out, clock_1_out, d_ff_1_q, d_ff_2_q, d_ff_3_q, d_ff_5_q, d_ff_7_q, d_ff_9_q, d_ff_11_q,
       d_ff_12_q, full_adder_1_carry_out, full_adder_1_sum, full_adder_2_carry_out, full_adder_2_sum,
       full_adder_3_carry_out, full_adder_3_sum, full_adder_4_carry_out, full_adder_4_sum, nor_1_out,
       not_1_out, xor_1_out, xor_2_out, xor_3_out, xor_4_out;

  Clock clock_1 (.out(clock_1_out));
  D_Flip_Flop d_ff_1 (.D(L_In_S), .clk(clock_1_out), .Q(d_ff_1_q));  // open: Qn, preset, reset
  D_Flip_Flop d_ff_2 (.D(L_In_2), .clk(clock_1_out), .Q(d_ff_2_q));  // open: Qn, preset, reset
  D_Flip_Flop d_ff_3 (.D(L_In_1), .clk(clock_1_out), .Q(d_ff_3_q));  // open: Qn, preset, reset
  Full_Adder full_adder_1 (
    .Carry_In(full_adder_2_carry_out), .R_In(xor_1_out), .L_In(d_ff_1_q), .Sum(full_adder_1_sum),
    .Carry_Out(full_adder_1_carry_out));
  not not_1 (not_1_out, Add_Sub_Command);
  and and_1 (and_1_out, not_1_out, full_adder_1_carry_out);
  D_Flip_Flop d_ff_4 (.D(full_adder_1_sum), .clk(clock_1_out), .Q(A_Out_S));  // open: Qn, preset, reset
  D_Flip_Flop d_ff_5 (.D(L_In_0), .clk(clock_1_out), .Q(d_ff_5_q));  // open: Qn, preset, reset
  Full_Adder full_adder_2 (
    .Carry_In(full_adder_3_carry_out), .R_In(xor_2_out), .L_In(d_ff_2_q), .Sum(full_adder_2_sum),
    .Carry_Out(full_adder_2_carry_out));
  D_Flip_Flop d_ff_6 (.D(full_adder_2_sum), .clk(clock_1_out), .Q(A_Out_2));  // open: Qn, preset, reset
  D_Flip_Flop d_ff_7 (.D(R_In_S), .clk(clock_1_out), .Q(d_ff_7_q));  // open: Qn, preset, reset
  Full_Adder full_adder_3 (
    .Carry_In(full_adder_4_carry_out), .R_In(xor_3_out), .L_In(d_ff_3_q), .Sum(full_adder_3_sum),
    .Carry_Out(full_adder_3_carry_out));
  D_Flip_Flop d_ff_8 (.D(full_adder_3_sum), .clk(clock_1_out), .Q(A_Out_1));  // open: Qn, preset, reset
  D_Flip_Flop d_ff_9 (.D(R_In_2), .clk(clock_1_out), .Q(d_ff_9_q));  // open: Qn, preset, reset
  xor xor_1 (xor_1_out, Add_Sub_Command, d_ff_7_q);
  Full_Adder full_adder_4 (
    .Carry_In(Add_Sub_Command), .R_In(xor_4_out), .L_In(d_ff_5_q), .Sum(full_adder_4_sum),
    .Carry_Out(full_adder_4_carry_out));
  D_Flip_Flop d_ff_10 (.D(full_adder_4_sum), .clk(clock_1_out), .Q(A_Out_0));  // open: Qn, preset, reset
  D_Flip_Flop d_ff_11 (.D(R_In_1), .clk(clock_1_out), .Q(d_ff_11_q));  // open: Qn, preset, reset
  xor xor_2 (xor_2_out, Add_Sub_Command, d_ff_9_q);
  D_Flip_Flop d_ff_12 (.D(R_In_0), .clk(clock_1_out), .Q(d_ff_12_q));  // open: Qn, preset, reset
  xor xor_3 (xor_3_out, Add_Sub_Command, d_ff_11_q);
  xor xor_4 (xor_4_out, Add_Sub_Command, d_ff_12_q);
  nor nor_1 (nor_1_out, full_adder_1_sum, full_adder_2_sum, full_adder_3_sum, full_adder_4_sum);
  D_Flip_Flop d_ff_13 (.D(full_adder_1_sum), .clk(clock_1_out), .Q(Negative));  // open: Qn, preset, reset
  D_Flip_Flop d_ff_14 (.D(nor_1_out), .clk(clock_1_out), .Q(Zero));  // open: Qn, preset, reset
  D_Flip_Flop d_ff_15 (.D(and_1_out), .clk(clock_1_out), .Q(Magnitude_Overflow));  // open: Qn, preset, reset

  // Notes on the sheet:
  //   L Register
  //   A-Out Register
  //   R Register
  //   Status Register
endmodule

module Full_Adder (
  input  Carry_In,
  input  R_In,
  input  L_In,
  output Sum,
  output Carry_Out
);

  wire and_1_out, and_2_out, xor_1_out;

  and and_1 (and_1_out, R_In, L_In);
  xor xor_1 (xor_1_out, R_In, L_In);
  and and_2 (and_2_out, xor_1_out, Carry_In);
  xor xor_2 (Sum, Carry_In, xor_1_out);
  or or_1 (Carry_Out, and_1_out, and_2_out);
endmodule
