// Logisim project basic_pipeline_CPU.circ as structural Verilog
module main (
  output Zero,
  output Neg,
  output Overflow
);

  wire Add_Sub, alu_1_aout0, alu_1_aout1, alu_1_aout2, alu_1_aout3, ALU_Src, and_2_out, and_3_out, and_4_out,
       Clck, clock_1_out, d_ff_1_q, d_ff_2_q, d_ff_3_q, d_ff_4_q, d_ff_5_q, d_ff_6_q, d_ff_7_q,
       data_ram_1_out0, data_ram_1_out1, data_ram_1_out2, data_ram_1_out3, Dest_Reg, HALT,
       incrementor_1_out0, incrementor_1_out1, incrementor_1_out2, instruction_ram_1_out0,
       instruction_ram_1_out1, instruction_ram_1_out2, instruction_ram_1_out3, JUMP, L_Selector_out0,
       L_Selector_out1, L_Selector_out2, L_Selector_out3, LoadEn, multiplexer_1_out, multiplexer_2_out,
       not_1_out, or_1_out, or_2_out, or_3_out, R_Selector_out0, R_Selector_out1, R_Selector_out2,
       R_Selector_out3, RAM_Address, Reg2, reg_block_1_out0, reg_block_1_out1, reg_block_1_out2,
       reg_block_1_out3, reg_block_1_r0_0, reg_block_1_r0_1, reg_block_1_r0_2, reg_block_1_r0_3,
       reg_block_1_r1_0, reg_block_1_r1_1, reg_block_1_r1_2, reg_block_1_r1_3, SaveEn,
       selector_8to4_2_1_out0, selector_8to4_2_1_out1, selector_8to4_2_1_out2, selector_8to4_2_1_out3,
       Single_Reg;

  D_Flip_Flop #(.trigger("falling")) d_ff_1 (
    .D(incrementor_1_out2), .clk(Clck), .Q(d_ff_1_q));  // open: Qn, preset, reset
  D_Flip_Flop #(.trigger("falling")) d_ff_2 (
    .D(incrementor_1_out1), .clk(Clck), .Q(d_ff_2_q));  // open: Qn, preset, reset
  D_Flip_Flop #(.trigger("falling")) d_ff_3 (
    .D(incrementor_1_out0), .clk(Clck), .Q(d_ff_3_q));  // open: Qn, preset, reset
  Clock clock_1 (.out(clock_1_out));
  and and_1 (Clck, clock_1_out, ~HALT);  // AND_Gate
  Incrementor incrementor_1 (
    .In2(d_ff_1_q), .In1(d_ff_2_q), .In0(d_ff_3_q), .Clock(Clck), .Out2(incrementor_1_out2),
    .Out1(incrementor_1_out1), .Out0(incrementor_1_out0));  // open: out_8
  Instruction_RAM instruction_ram_1 (
    .Clock(Clck), .a2(d_ff_1_q), .a1(d_ff_2_q), .a0(d_ff_3_q), .Out3(instruction_ram_1_out3),
    .Out2(instruction_ram_1_out2), .Out1(instruction_ram_1_out1), .Out0(instruction_ram_1_out0));
  D_Flip_Flop #(.trigger("falling")) d_ff_4 (
    .D(instruction_ram_1_out3), .clk(Clck), .Q(d_ff_4_q));  // open: Qn, preset, reset
  D_Flip_Flop #(.trigger("falling")) d_ff_5 (
    .D(instruction_ram_1_out2), .clk(Clck), .Q(d_ff_5_q));  // open: Qn, preset, reset
  D_Flip_Flop #(.trigger("falling")) d_ff_6 (
    .D(instruction_ram_1_out1), .clk(Clck), .Q(d_ff_6_q));  // open: Qn, preset, reset
  D_Flip_Flop #(.trigger("falling")) d_ff_7 (
    .D(instruction_ram_1_out0), .clk(Clck), .Q(d_ff_7_q));  // open: Qn, preset, reset
  Multiplexer multiplexer_1 (.in0(Single_Reg), .in1(Dest_Reg), .out(multiplexer_1_out), .sel(ALU_Src));
  Multiplexer multiplexer_2 (.in0(SaveEn), .in1(1'b1), .out(multiplexer_2_out), .sel(ALU_Src));
  or or_1 (or_1_out, ALU_Src, LoadEn, SaveEn);
  and and_2 (and_2_out, Clck, or_1_out);
  Reg_Block reg_block_1 (
    .Clock(and_2_out), .R0_R1(multiplexer_1_out), .Mode(multiplexer_2_out), .In3(selector_8to4_2_1_out3),
    .In2(selector_8to4_2_1_out2), .In1(selector_8to4_2_1_out1), .In0(selector_8to4_2_1_out0),
    .R1_3(reg_block_1_r1_3), .R1_2(reg_block_1_r1_2), .R1_1(reg_block_1_r1_1), .R1_0(reg_block_1_r1_0),
    .Out3(reg_block_1_out3), .Out2(reg_block_1_out2), .Out1(reg_block_1_out1), .Out0(reg_block_1_out0),
    .R0_3(reg_block_1_r0_3), .R0_2(reg_block_1_r0_2), .R0_1(reg_block_1_r0_1), .R0_0(reg_block_1_r0_0));
  CU cu_1 (
    .OpCode3(d_ff_4_q), .OpCode2(d_ff_5_q), .OpCode1(d_ff_6_q), .OpCode0(d_ff_7_q), .JUMP(JUMP),
    .LoadEn(LoadEn), .SaveEn(SaveEn), .Single_Reg(Single_Reg), .RAM_Address(RAM_Address), .ALU_Src(ALU_Src),
    .Add_Sub(Add_Sub), .Dest_Reg(Dest_Reg), .Reg2(Reg2), .HALT(HALT));
  Selector_8to4 L_Selector (
    .A_In3(reg_block_1_r0_3), .A_In2(reg_block_1_r0_2), .A_In1(reg_block_1_r0_1), .A_In0(reg_block_1_r0_0),
    .B_In3(reg_block_1_r1_3), .B_In2(reg_block_1_r1_2), .B_In1(reg_block_1_r1_1), .B_In0(reg_block_1_r1_0),
    .Select_bit(Dest_Reg), .Out3(L_Selector_out3), .Out2(L_Selector_out2), .Out1(L_Selector_out1),
    .Out0(L_Selector_out0));
  Selector_8to4 R_Selector (
    .A_In3(reg_block_1_r0_3), .A_In2(reg_block_1_r0_2), .A_In1(reg_block_1_r0_1), .A_In0(reg_block_1_r0_0),
    .B_In3(reg_block_1_r1_3), .B_In2(reg_block_1_r1_2), .B_In1(reg_block_1_r1_1), .B_In0(reg_block_1_r1_0),
    .Select_bit(Reg2), .Out3(R_Selector_out3), .Out2(R_Selector_out2), .Out1(R_Selector_out1),
    .Out0(R_Selector_out0));
  ALU alu_1 (
    .RIn0(R_Selector_out0), .Command(Add_Sub), .LIn3(L_Selector_out3), .LIn2(L_Selector_out2),
    .LIn1(L_Selector_out1), .LIn0(L_Selector_out0), .RIn3(R_Selector_out3), .RIn2(R_Selector_out2),
    .RIn1(R_Selector_out1), .Zero(Zero), .Negative(Neg), .Overflow(Overflow), .AOut3(alu_1_aout3),
    .AOut2(alu_1_aout2), .AOut1(alu_1_aout1), .AOut0(alu_1_aout0));
  not not_1 (not_1_out, ALU_Src);
  Selector_8to4_2 selector_8to4_2_1 (
    .A_In3(alu_1_aout3), .A_In2(alu_1_aout2), .A_In1(alu_1_aout1), .A_In0(alu_1_aout0),
    .B_In3(data_ram_1_out3), .B_In2(data_ram_1_out2), .B_In1(data_ram_1_out1), .B_In0(data_ram_1_out0),
    .Clock(and_3_out), .Select_bit(not_1_out), .Out3(selector_8to4_2_1_out3), .Out2(selector_8to4_2_1_out2),
    .Out1(selector_8to4_2_1_out1), .Out0(selector_8to4_2_1_out0));
  and and_3 (and_3_out, Clck, or_2_out);
  or or_2 (or_2_out, ALU_Src, LoadEn);
  and and_4 (and_4_out, Clck, or_3_out);
  or or_3 (or_3_out, SaveEn, LoadEn);
  Data_RAM data_ram_1 (
    .In3(reg_block_1_out3), .In2(reg_block_1_out2), .In1(reg_block_1_out1), .In0(reg_block_1_out0),
    .Address(RAM_Address), .Mode(LoadEn), .Clock(and_4_out), .Out3(data_ram_1_out3), .Out2(data_ram_1_out2),
    .Out1(data_ram_1_out1), .Out0(data_ram_1_out0));

  // Notes on the sheet:
  //   PC
  //   Main Clock
  //   Starting address and all Instructions should be inputted manually
  //   directly in the PC flip-flops and whithin the Instruction_RAM sub-circuit.
  //   IR
  //   ALU Status
  //   Data should be inputted manually whithin the Data_RAM sub-circuit.
endmodule

module Fill_Adder (
  input  A,
  input  B,
  input  Carry,
  output C,
  output Sum
);

  wire and_1_out, and_2_out, xor_1_out;

  and and_1 (and_1_out, A, B);
  xor xor_1 (xor_1_out, A, B);
  and and_2 (and_2_out, xor_1_out, Carry);
  or or_1 (C, and_1_out, and_2_out);
  xor xor_2 (Sum, xor_1_out, Carry);
endmodule

module Instruction_RAM (
  input  Clock,
  input  a2,
  input  a1,
  input  a0,
  output Out3,
  output Out2,
  output Out1,
  output Out0
);

  wire and_1_out, and_2_out, and_3_out, and_4_out, and_5_out, and_6_out, and_7_out, and_8_out, and_9_out,
       and_10_out, and_11_out, and_12_out, and_13_out, and_14_out, and_15_out, and_16_out, and_17_out,
       and_18_out, and_19_out, and_20_out, and_21_out, and_22_out, and_23_out, and_24_out, and_25_out,
       and_26_out, and_27_out, and_28_out, and_29_out, and_30_out, and_31_out, and_32_out, and_33_out,
       and_34_out, and_35_out, and_36_out, and_37_out, and_38_out, and_39_out, and_40_out, d_ff_1_q,
       d_ff_2_q, d_ff_3_q, d_ff_4_q, d_ff_5_q, d_ff_6_q, d_ff_7_q, d_ff_8_q, d_ff_9_q, d_ff_10_q, d_ff_11_q,
       d_ff_12_q, d_ff_13_q, d_ff_14_q, d_ff_15_q, d_ff_16_q, d_ff_17_q, d_ff_18_q, d_ff_19_q, d_ff_20_q,
       d_ff_21_q, d_ff_22_q, d_ff_23_q, d_ff_24_q, d_ff_25_q, d_ff_26_q, d_ff_27_q, d_ff_28_q, d_ff_29_q,
       d_ff_30_q, d_ff_31_q, d_ff_32_q, not_1_out, not_2_out, not_3_out, not_4_out, not_5_out, not_6_out,
       not_7_out, not_8_out, not_9_out, not_10_out, not_11_out, not_12_out;

  not not_1 (not_1_out, a0);
  not not_2 (not_2_out, a1);
  not not_3 (not_3_out, a1);
  not not_4 (not_4_out, a0);
  not not_5 (not_5_out, a2);
  not not_6 (not_6_out, a2);
  not not_7 (not_7_out, a0);
  not not_8 (not_8_out, a2);
  not not_9 (not_9_out, a1);
  not not_10 (not_10_out, a2);
  not not_11 (not_11_out, a1);
  not not_12 (not_12_out, a0);
  and and_1 (and_1_out, a2, a1, Clock, a0);
  and and_2 (and_2_out, a2, a1, Clock, not_1_out);
  and and_3 (and_3_out, a2, not_2_out, Clock, a0);
  and and_4 (and_4_out, a2, not_3_out, Clock, not_4_out);
  and and_5 (and_5_out, not_5_out, a1, Clock, a0);
  and and_6 (and_6_out, not_6_out, a1, Clock, not_7_out);
  and and_7 (and_7_out, not_8_out, not_9_out, Clock, a0);
  and and_8 (and_8_out, not_10_out, not_11_out, Clock, not_12_out);
  D_Flip_Flop #(.trigger("high")) d_ff_1 (.clk(and_1_out), .Q(d_ff_1_q));  // open: D, Qn, preset, reset
  D_Flip_Flop #(.trigger("high")) d_ff_2 (.clk(and_2_out), .Q(d_ff_2_q));  // open: D, Qn, preset, reset
  D_Flip_Flop #(.trigger("high")) d_ff_3 (.clk(and_3_out), .Q(d_ff_3_q));  // open: D, Qn, preset, reset
  D_Flip_Flop #(.trigger("high")) d_ff_4 (.clk(and_4_out), .Q(d_ff_4_q));  // open: D, Qn, preset, reset
  D_Flip_Flop #(.trigger("high")) d_ff_5 (.clk(and_5_out), .Q(d_ff_5_q));  // open: D, Qn, preset, reset
  D_Flip_Flop #(.trigger("high")) d_ff_6 (.clk(and_6_out), .Q(d_ff_6_q));  // open: D, Qn, preset, reset
  D_Flip_Flop #(.trigger("high")) d_ff_7 (.clk(and_7_out), .Q(d_ff_7_q));  // open: D, Qn, preset, reset
  and and_9 (and_9_out, d_ff_1_q, and_1_out);
  and and_10 (and_10_out, d_ff_2_q, and_2_out);
  and and_11 (and_11_out, d_ff_3_q, and_3_out);
  and and_12 (and_12_out, d_ff_4_q, and_4_out);
  and and_13 (and_13_out, d_ff_5_q, and_5_out);
  and and_14 (and_14_out, d_ff_6_q, and_6_out);
  and and_15 (and_15_out, d_ff_7_q, and_7_out);
  and and_16 (and_16_out, d_ff_8_q, and_8_out);
  D_Flip_Flop #(.trigger("high")) d_ff_8 (.clk(and_8_out), .Q(d_ff_8_q));  // open: D, Qn, preset, reset
  or or_1 (Out3, and_9_out, and_10_out, and_11_out, and_12_out, and_13_out, and_14_out, and_15_out, and_16_out);
  D_Flip_Flop #(.trigger("high")) d_ff_9 (.clk(and_1_out), .Q(d_ff_9_q));  // open: D, Qn, preset, reset
  D_Flip_Flop #(.trigger("high")) d_ff_10 (.clk(and_2_out), .Q(d_ff_10_q));  // open: D, Qn, preset, reset
  D_Flip_Flop #(.trigger("high")) d_ff_11 (.clk(and_3_out), .Q(d_ff_11_q));  // open: D, Qn, preset, reset
  D_Flip_Flop #(.trigger("high")) d_ff_12 (.clk(and_4_out), .Q(d_ff_12_q));  // open: D, Qn, preset, reset
  D_Flip_Flop #(.trigger("high")) d_ff_13 (.clk(and_5_out), .Q(d_ff_13_q));  // open: D, Qn, preset, reset
  D_Flip_Flop #(.trigger("high")) d_ff_14 (.clk(and_6_out), .Q(d_ff_14_q));  // open: D, Qn, preset, reset
  D_Flip_Flop #(.trigger("high")) d_ff_15 (.clk(and_7_out), .Q(d_ff_15_q));  // open: D, Qn, preset, reset
  D_Flip_Flop #(.trigger("high")) d_ff_16 (.clk(and_8_out), .Q(d_ff_16_q));  // open: D, Qn, preset, reset
  or or_2 (Out2, and_17_out, and_18_out, and_19_out, and_20_out, and_21_out, and_22_out, and_23_out, and_24_out);
  and and_17 (and_17_out, d_ff_9_q, and_1_out);
  and and_18 (and_18_out, d_ff_10_q, and_2_out);
  and and_19 (and_19_out, d_ff_11_q, and_3_out);
  and and_20 (and_20_out, d_ff_12_q, and_4_out);
  and and_21 (and_21_out, d_ff_13_q, and_5_out);
  and and_22 (and_22_out, d_ff_14_q, and_6_out);
  and and_23 (and_23_out, d_ff_15_q, and_7_out);
  and and_24 (and_24_out, d_ff_16_q, and_8_out);
  D_Flip_Flop #(.trigger("high")) d_ff_17 (.clk(and_1_out), .Q(d_ff_17_q));  // open: D, Qn, preset, reset
  D_Flip_Flop #(.trigger("high")) d_ff_18 (.clk(and_2_out), .Q(d_ff_18_q));  // open: D, Qn, preset, reset
  D_Flip_Flop #(.trigger("high")) d_ff_19 (.clk(and_3_out), .Q(d_ff_19_q));  // open: D, Qn, preset, reset
  D_Flip_Flop #(.trigger("high")) d_ff_20 (.clk(and_4_out), .Q(d_ff_20_q));  // open: D, Qn, preset, reset
  D_Flip_Flop #(.trigger("high")) d_ff_21 (.clk(and_5_out), .Q(d_ff_21_q));  // open: D, Qn, preset, reset
  D_Flip_Flop #(.trigger("high")) d_ff_22 (.clk(and_6_out), .Q(d_ff_22_q));  // open: D, Qn, preset, reset
  D_Flip_Flop #(.trigger("high")) d_ff_23 (.clk(and_7_out), .Q(d_ff_23_q));  // open: D, Qn, preset, reset
  D_Flip_Flop #(.trigger("high")) d_ff_24 (.clk(and_8_out), .Q(d_ff_24_q));  // open: D, Qn, preset, reset
  or or_3 (Out1, and_25_out, and_26_out, and_27_out, and_28_out, and_29_out, and_30_out, and_31_out, and_32_out);
  and and_25 (and_25_out, d_ff_17_q, and_1_out);
  and and_26 (and_26_out, d_ff_18_q, and_2_out);
  and and_27 (and_27_out, d_ff_19_q, and_3_out);
  and and_28 (and_28_out, d_ff_20_q, and_4_out);
  and and_29 (and_29_out, d_ff_21_q, and_5_out);
  and and_30 (and_30_out, d_ff_22_q, and_6_out);
  and and_31 (and_31_out, d_ff_23_q, and_7_out);
  and and_32 (and_32_out, d_ff_24_q, and_8_out);
  and and_33 (and_33_out, d_ff_25_q, and_1_out);
  D_Flip_Flop #(.trigger("high")) d_ff_25 (.clk(and_1_out), .Q(d_ff_25_q));  // open: D, Qn, preset, reset
  and and_34 (and_34_out, d_ff_26_q, and_2_out);
  D_Flip_Flop #(.trigger("high")) d_ff_26 (.clk(and_2_out), .Q(d_ff_26_q));  // open: D, Qn, preset, reset
  and and_35 (and_35_out, d_ff_27_q, and_3_out);
  D_Flip_Flop #(.trigger("high")) d_ff_27 (.clk(and_3_out), .Q(d_ff_27_q));  // open: D, Qn, preset, reset
  and and_36 (and_36_out, d_ff_28_q, and_4_out);
  D_Flip_Flop #(.trigger("high")) d_ff_28 (.clk(and_4_out), .Q(d_ff_28_q));  // open: D, Qn, preset, reset
  and and_37 (and_37_out, d_ff_29_q, and_5_out);
  D_Flip_Flop #(.trigger("high")) d_ff_29 (.clk(and_5_out), .Q(d_ff_29_q));  // open: D, Qn, preset, reset
  and and_38 (and_38_out, d_ff_30_q, and_6_out);
  D_Flip_Flop #(.trigger("high")) d_ff_30 (.clk(and_6_out), .Q(d_ff_30_q));  // open: D, Qn, preset, reset
  and and_39 (and_39_out, d_ff_31_q, and_7_out);
  D_Flip_Flop #(.trigger("high")) d_ff_31 (.clk(and_7_out), .Q(d_ff_31_q));  // open: D, Qn, preset, reset
  and and_40 (and_40_out, d_ff_32_q, and_8_out);
  D_Flip_Flop #(.trigger("high")) d_ff_32 (.clk(and_8_out), .Q(d_ff_32_q));  // open: D, Qn, preset, reset
  or or_4 (Out0, and_33_out, and_34_out, and_35_out, and_36_out, and_37_out, and_38_out, and_39_out, and_40_out);

  // Notes on the sheet:
  //   3-bit address input pins
  //   4-bit data output pins
endmodule

module Incrementor (
  input  In2,
  input  In1,
  input  In0,
  input  Clock,
  output Out2,
  output Out1,
  output Out0,
  output out_8
);

  wire fill_adder_1_sum, fill_adder_2_c, fill_adder_2_sum, fill_adder_3_c, fill_adder_3_sum;

  Fill_Adder fill_adder_1 (.A(In2), .Carry(fill_adder_2_c), .C(out_8), .Sum(fill_adder_1_sum));  // open: B
  Fill_Adder fill_adder_2 (.A(In1), .Carry(fill_adder_3_c), .C(fill_adder_2_c), .Sum(fill_adder_2_sum));  // open: B
  Fill_Adder fill_adder_3 (.A(In0), .B(1'b1), .C(fill_adder_3_c), .Sum(fill_adder_3_sum));  // open: Carry
  D_Flip_Flop #(.trigger("falling")) d_ff_1 (.D(fill_adder_1_sum), .clk(Clock), .Q(Out2));  // open: Qn, preset, reset
  D_Flip_Flop #(.trigger("falling")) d_ff_2 (.D(fill_adder_2_sum), .clk(Clock), .Q(Out1));  // open: Qn, preset, reset
  D_Flip_Flop #(.trigger("falling")) d_ff_3 (.D(fill_adder_3_sum), .clk(Clock), .Q(Out0));  // open: Qn, preset, reset
endmodule

module CU (
  input  OpCode3,
  input  OpCode2,
  input  OpCode1,
  input  OpCode0,
  output JUMP,
  output LoadEn,
  output SaveEn,
  output Single_Reg,
  output RAM_Address,
  output ALU_Src,
  output Add_Sub,
  output Dest_Reg,
  output Reg2,
  output HALT
);

  wire and_2_out, and_6_out, and_7_out, and_8_out;

  and and_1 (JUMP, ~OpCode0, ~OpCode1, ~OpCode2, ~OpCode3);  // AND_Gate
  and and_2 (and_2_out, ~OpCode3, ~OpCode2);  // AND_Gate
  and and_3 (SaveEn, ~OpCode3, OpCode2);  // AND_Gate
  and and_4 (Single_Reg, ~OpCode3, OpCode1);  // AND_Gate
  and and_5 (RAM_Address, ~OpCode3, OpCode0);  // AND_Gate
  and and_6 (and_6_out, OpCode3, OpCode2);
  and and_7 (and_7_out, OpCode3, OpCode1);
  and and_8 (and_8_out, OpCode3, OpCode0);
  and and_9 (HALT, OpCode0, OpCode1, OpCode2, OpCode3);
  and and_10 (LoadEn, ~JUMP, and_2_out);  // AND_Gate
  and and_11 (ALU_Src, ~HALT, OpCode3);  // AND_Gate
  and and_12 (Add_Sub, ~HALT, and_6_out);  // AND_Gate
  and and_13 (Dest_Reg, ~HALT, and_7_out);  // AND_Gate
  and and_14 (Reg2, ~HALT, and_8_out);  // AND_Gate
endmodule

module ALU (
  input  Command,
  input  LIn3,
  input  LIn2,
  input  LIn1,
  input  LIn0,
  input  RIn3,
  input  RIn2,
  input  RIn1,
  input  RIn0,
  output Zero,
  output Negative,
  output Overflow,
  output AOut3,
  output AOut2,
  output AOut1,
  output AOut0
);

  wire and_1_out, and_2_out, and_3_out, and_4_out, and_5_out, and_6_out, and_8_out, and_9_out, and_10_out,
       and_11_out, and_12_out, and_13_out, and_14_out, and_15_out, and_16_out, and_17_out, and_18_out,
       fill_adder_1_c, fill_adder_2_c, fill_adder_3_c, Neg_out, not_1_out, not_2_out, not_3_out, not_4_out,
       not_5_out, not_6_out, not_7_out, not_8_out, not_9_out, not_10_out, not_11_out, not_12_out, not_13_out,
       not_14_out, not_15_out, or_1_out, or_2_out, or_3_out, or_4_out, or_5_out, Pos_out, xor_2_out,
       xor_3_out, xor_4_out, xor_5_out;

  not not_1 (not_1_out, Command);
  Fill_Adder fill_adder_1 (.A(or_1_out), .B(LIn3), .Carry(fill_adder_2_c), .C(fill_adder_1_c), .Sum(AOut3));
  Fill_Adder fill_adder_2 (.A(or_2_out), .B(LIn2), .Carry(fill_adder_3_c), .C(fill_adder_2_c), .Sum(AOut2));
  or or_1 (or_1_out, xor_2_out, and_2_out);
  Fill_Adder fill_adder_3 (.A(or_3_out), .B(LIn1), .Carry(and_1_out), .C(fill_adder_3_c), .Sum(AOut1));
  or or_2 (or_2_out, xor_3_out, and_4_out);
  or or_3 (or_3_out, xor_4_out, and_5_out);
  and and_1 (and_1_out, LIn0, or_4_out);
  xor xor_1 (AOut0, LIn0, or_4_out);
  and and_2 (and_2_out, RIn3, not_1_out);
  and and_3 (and_3_out, not_6_out, and_6_out);
  or or_4 (or_4_out, xor_5_out, and_8_out);
  not not_2 (not_2_out, AOut0);
  not not_3 (not_3_out, AOut1);
  not not_4 (not_4_out, AOut2);
  not not_5 (not_5_out, AOut3);
  and and_4 (and_4_out, RIn2, not_1_out);
  and and_5 (and_5_out, RIn1, not_1_out);
  xor xor_2 (xor_2_out, not_6_out, and_6_out);
  and and_6 (and_6_out, not_11_out, and_10_out);
  and and_7 (Zero, not_2_out, not_3_out, not_4_out, not_5_out);
  and and_8 (and_8_out, RIn0, not_1_out);
  and and_9 (and_9_out, RIn3, Command);
  not not_6 (not_6_out, and_9_out);
  xor xor_3 (xor_3_out, not_11_out, and_10_out);
  and and_10 (and_10_out, not_12_out, and_14_out);
  not not_7 (not_7_out, or_1_out);
  not not_8 (not_8_out, LIn3);
  not not_9 (not_9_out, or_1_out);
  and and_11 (and_11_out, RIn0, Command);
  and and_12 (and_12_out, RIn2, Command);
  and and_13 (and_13_out, RIn1, Command);
  not not_10 (not_10_out, and_11_out);
  not not_11 (not_11_out, and_12_out);
  not not_12 (not_12_out, and_13_out);
  and and_14 (and_14_out, not_10_out, 1'b1);
  xor xor_4 (xor_4_out, not_12_out, and_14_out);
  and Neg (Neg_out, or_1_out, LIn3);
  and Pos (Pos_out, not_7_out, not_8_out);
  xor xor_5 (xor_5_out, not_10_out, 1'b1);
  and and_15 (and_15_out, AOut3, Neg_out);
  and and_16 (and_16_out, Pos_out, AOut3);
  and and_17 (and_17_out, not_13_out, not_9_out, fill_adder_1_c);
  not not_13 (not_13_out, Command);
  not not_14 (not_14_out, fill_adder_1_c);
  and and_18 (and_18_out, and_15_out, not_14_out);
  or or_5 (or_5_out, and_17_out, and_16_out, and_18_out);
  not not_15 (not_15_out, Zero);
  and notZero (Overflow, or_5_out, not_15_out);

  assign Negative = AOut3;

  // Other names for the same wires on the sheet: CMD = Command

  // Notes on the sheet:
  //   B Input
  //   L input
  //   A-out output
  //   A Input
  //   Adder
  //   R Input
  //   2's Complement
  //   Status output
  //   -8 + -8 is underflow (not supported)
endmodule

module Data_RAM (
  input  In3,
  input  In2,
  input  In1,
  input  In0,
  input  Address,
  input  Mode,
  input  Clock,
  output Out3,
  output Out2,
  output Out1,
  output Out0
);

  wire and_1_out, and_2_out, and_3_out, and_4_out, and_5_out, and_6_out, and_7_out, and_8_out, and_9_out,
       and_10_out, and_11_out, and_12_out, and_13_out, and_14_out, and_15_out, and_16_out, and_17_out,
       and_18_out, and_19_out, and_20_out, d_ff_1_q, d_ff_2_q, d_ff_3_q, d_ff_4_q, d_ff_5_q, d_ff_6_q,
       d_ff_7_q, d_ff_8_q, not_1_out, not_2_out;

  and and_1 (and_1_out, Clock, Address);
  not not_1 (not_1_out, Address);
  and and_2 (and_2_out, and_1_out, not_2_out);
  and and_3 (and_3_out, Clock, not_1_out);
  and and_4 (and_4_out, and_3_out, not_2_out);
  not not_2 (not_2_out, Mode);
  and and_5 (and_5_out, and_1_out, not_2_out, In3);
  D_Flip_Flop #(.trigger("high")) d_ff_1 (.D(and_5_out), .clk(and_2_out), .Q(d_ff_1_q));  // open: Qn, preset, reset
  and and_6 (and_6_out, and_3_out, not_2_out, In3);
  D_Flip_Flop #(.trigger("high")) d_ff_2 (.D(and_6_out), .clk(and_4_out), .Q(d_ff_2_q));  // open: Qn, preset, reset
  and and_7 (and_7_out, d_ff_1_q, and_1_out, Mode);
  and and_8 (and_8_out, d_ff_2_q, and_3_out, Mode);
  or or_1 (Out3, and_7_out, and_8_out);
  and and_9 (and_9_out, and_1_out, not_2_out, In2);
  D_Flip_Flop #(.trigger("high")) d_ff_3 (.D(and_9_out), .clk(and_2_out), .Q(d_ff_3_q));  // open: Qn, preset, reset
  and and_10 (and_10_out, and_3_out, not_2_out, In2);
  D_Flip_Flop #(.trigger("high")) d_ff_4 (.D(and_10_out), .clk(and_4_out), .Q(d_ff_4_q));  // open: Qn, preset, reset
  or or_2 (Out2, and_11_out, and_12_out);
  and and_11 (and_11_out, d_ff_3_q, and_1_out, Mode);
  and and_12 (and_12_out, d_ff_4_q, and_3_out, Mode);
  and and_13 (and_13_out, and_1_out, not_2_out, In1);
  and and_14 (and_14_out, and_3_out, not_2_out, In1);
  and and_15 (and_15_out, d_ff_5_q, and_1_out, Mode);
  D_Flip_Flop #(.trigger("high")) d_ff_5 (.D(and_13_out), .clk(and_2_out), .Q(d_ff_5_q));  // open: Qn, preset, reset
  and and_16 (and_16_out, d_ff_6_q, and_3_out, Mode);
  D_Flip_Flop #(.trigger("high")) d_ff_6 (.D(and_14_out), .clk(and_4_out), .Q(d_ff_6_q));  // open: Qn, preset, reset
  or or_3 (Out1, and_15_out, and_16_out);
  and and_17 (and_17_out, and_1_out, not_2_out, In0);
  D_Flip_Flop #(.trigger("high")) d_ff_7 (.D(and_17_out), .clk(and_2_out), .Q(d_ff_7_q));  // open: Qn, preset, reset
  and and_18 (and_18_out, and_3_out, not_2_out, In0);
  D_Flip_Flop #(.trigger("high")) d_ff_8 (.D(and_18_out), .clk(and_4_out), .Q(d_ff_8_q));  // open: Qn, preset, reset
  or or_4 (Out0, and_19_out, and_20_out);
  and and_19 (and_19_out, d_ff_7_q, and_1_out, Mode);
  and and_20 (and_20_out, d_ff_8_q, and_3_out, Mode);

  // Notes on the sheet:
  //   Mode input pin
  //   4-bit data input pins
  //   4-bit data output pins
endmodule

module Reg_Block (
  input  Clock,
  input  R0_R1,
  input  Mode,
  input  In3,
  input  In2,
  input  In1,
  input  In0,
  output Out3,
  output Out2,
  output Out1,
  output Out0,
  output R0_3,
  output R0_2,
  output R0_1,
  output R0_0,
  output R1_3,
  output R1_2,
  output R1_1,
  output R1_0
);

  wire and_1_out, and_2_out, and_3_out, and_4_out, and_5_out, and_6_out, and_7_out, and_8_out, and_9_out,
       and_10_out, and_11_out, and_12_out, and_13_out, and_14_out, and_15_out, and_16_out, and_17_out,
       and_18_out, and_19_out, and_20_out, not_1_out, not_2_out;

  and and_1 (and_1_out, Clock, R0_R1);
  and and_2 (and_2_out, Clock, not_1_out);
  not not_1 (not_1_out, R0_R1);
  and and_3 (and_3_out, and_1_out, not_2_out);
  and and_4 (and_4_out, and_2_out, not_2_out);
  not not_2 (not_2_out, Mode);
  and and_5 (and_5_out, and_1_out, not_2_out, In3);
  and and_6 (and_6_out, and_2_out, not_2_out, In3);
  and and_7 (and_7_out, R1_3, and_1_out, Mode);
  D_Flip_Flop #(.trigger("high")) d_ff_1 (.D(and_5_out), .clk(and_3_out), .Q(R1_3));  // open: Qn, preset, reset
  and and_8 (and_8_out, R0_3, and_2_out, Mode);
  D_Flip_Flop #(.trigger("high")) d_ff_2 (.D(and_6_out), .clk(and_4_out), .Q(R0_3));  // open: Qn, preset, reset
  or or_1 (Out3, and_7_out, and_8_out);
  and and_9 (and_9_out, and_1_out, not_2_out, In2);
  D_Flip_Flop #(.trigger("high")) d_ff_3 (.D(and_9_out), .clk(and_3_out), .Q(R1_2));  // open: Qn, preset, reset
  and and_10 (and_10_out, and_2_out, not_2_out, In2);
  D_Flip_Flop #(.trigger("high")) d_ff_4 (.D(and_10_out), .clk(and_4_out), .Q(R0_2));  // open: Qn, preset, reset
  or or_2 (Out2, and_11_out, and_12_out);
  and and_11 (and_11_out, R1_2, and_1_out, Mode);
  and and_12 (and_12_out, R0_2, and_2_out, Mode);
  and and_13 (and_13_out, and_1_out, not_2_out, In1);
  D_Flip_Flop #(.trigger("high")) d_ff_5 (.D(and_13_out), .clk(and_3_out), .Q(R1_1));  // open: Qn, preset, reset
  and and_14 (and_14_out, and_2_out, not_2_out, In1);
  D_Flip_Flop #(.trigger("high")) d_ff_6 (.D(and_14_out), .clk(and_4_out), .Q(R0_1));  // open: Qn, preset, reset
  or or_3 (Out1, and_15_out, and_16_out);
  and and_15 (and_15_out, R1_1, and_1_out, Mode);
  and and_16 (and_16_out, R0_1, and_2_out, Mode);
  and and_17 (and_17_out, and_1_out, not_2_out, In0);
  and and_18 (and_18_out, and_2_out, not_2_out, In0);
  D_Flip_Flop #(.trigger("high")) d_ff_7 (.D(and_17_out), .clk(and_3_out), .Q(R1_0));  // open: Qn, preset, reset
  D_Flip_Flop #(.trigger("high")) d_ff_8 (.D(and_18_out), .clk(and_4_out), .Q(R0_0));  // open: Qn, preset, reset
  or or_4 (Out0, and_19_out, and_20_out);
  and and_19 (and_19_out, R1_0, and_1_out, Mode);
  and and_20 (and_20_out, R0_0, and_2_out, Mode);

  // Notes on the sheet:
  //   1-bit address
  //   Mode input pin
  //   4-bit data input pins
endmodule

module Selector_8to4 (
  input  A_In3,
  input  A_In2,
  input  A_In1,
  input  A_In0,
  input  B_In3,
  input  B_In2,
  input  B_In1,
  input  B_In0,
  input  Select_bit,
  output Out3,
  output Out2,
  output Out1,
  output Out0
);

  Multiplexer multiplexer_1 (.in0(A_In3), .in1(B_In3), .out(Out3), .sel(Select_bit));
  Multiplexer multiplexer_2 (.in0(A_In2), .in1(B_In2), .out(Out2), .sel(Select_bit));
  Multiplexer multiplexer_3 (.in0(A_In1), .in1(B_In1), .out(Out1), .sel(Select_bit));
  Multiplexer multiplexer_4 (.in0(A_In0), .in1(B_In0), .out(Out0), .sel(Select_bit));
endmodule

module Selector_8to4_2 (
  input  A_In3,
  input  A_In2,
  input  A_In1,
  input  A_In0,
  input  B_In3,
  input  B_In2,
  input  B_In1,
  input  B_In0,
  input  Clock,
  input  Select_bit,
  output Out3,
  output Out2,
  output Out1,
  output Out0
);

  wire multiplexer_1_out, multiplexer_2_out, multiplexer_3_out, multiplexer_4_out;

  Multiplexer multiplexer_1 (.in0(A_In3), .in1(B_In3), .out(multiplexer_1_out), .sel(Select_bit));
  Multiplexer multiplexer_2 (.in0(A_In2), .in1(B_In2), .out(multiplexer_2_out), .sel(Select_bit));
  Multiplexer multiplexer_3 (.in0(A_In1), .in1(B_In1), .out(multiplexer_3_out), .sel(Select_bit));
  Multiplexer multiplexer_4 (.in0(A_In0), .in1(B_In0), .out(multiplexer_4_out), .sel(Select_bit));
  and and_1 (Out3, multiplexer_1_out, Clock);
  and and_2 (Out2, multiplexer_2_out, Clock);
  and and_3 (Out1, multiplexer_3_out, Clock);
  and and_4 (Out0, multiplexer_4_out, Clock);
endmodule
